// Logisim project datapath.circ as structural Verilog: 4 circuits, main circuit main
module main (
  output halt
);

  wire alu_1_zero, and_1_out, and_2_out, and_3_out, clock_1_out, clock_2_out, clock_3_out, clock_4_out,
       clock_5_out, comparator_2_eq, comparator_3_eq, memory_controller_1_p1, memory_controller_1_p9,
       memory_controller_1_p10, memory_controller_1_p11, memory_controller_1_p12, memory_controller_1_p13,
       not_1_out, not_2_out, not_3_out, not_4_out, not_5_out, or_1_out, or_2_out, xor_1_out, xor_2_out;
  wire [1:0] multiplexer_5_out;
  wire [3:0] multiplexer_2_out, ram_1_data;
  wire [6:0] bit_extender_1_out, keyboard_1_data;
  wire [13:0] memory_controller_1_p3;
  wire [15:0] adder_1_out, alu_1_result, bit_extender_2_out, memory_controller_1_p15, multiplexer_1_out,
       multiplexer_3_out, multiplexer_4_out, multiplexer_6_out, multiplexer_7_out, multiplexer_8_out,
       register_1_q, register_file_1_read_data_0, register_file_1_read_data_1, rom_1_data, shifter_1_data_out;
  wire [31:0] memory_controller_1_p2, ram_2_data;
  wire [31:4] ram_1_data_2;

  Register #(.width(16)) register_1 (
    .D(multiplexer_1_out), .en(not_1_out), .Q(register_1_q), .clk(clock_1_out));  // open: clr
  not not_1 (not_1_out, halt);
  Clock clock_1 (.out(clock_1_out));
  Comparator #(.width(16), .mode("unsigned")) comparator_1 (.a(register_1_q), .b(16'hff00), .eq(halt));  // open: gt, lt
  Adder #(.width(16)) adder_1 (.a(16'h4), .b(register_1_q), .out(adder_1_out));  // open: cin, cout
  Multiplexer #(.width(16), .enable("false")) multiplexer_1 (
    .in0(adder_1_out), .in1(multiplexer_3_out), .out(multiplexer_1_out), .sel(or_1_out));
  RAM #(.addrWidth(14), .dataWidth(32), .bus("separate")) ram_1 (
    .addr(register_1_q[15:2]), .data({ram_1_data_2, ram_1_data}));  // open: din, str, sel, clk, ld, clr
  ROM #(.addrWidth(4), .dataWidth(16)) rom_1 (.addr(ram_1_data_2[31:28]), .data(rom_1_data));  // open: sel
  Multiplexer #(.width(4), .enable("false")) multiplexer_2 (
    .in0(ram_1_data_2[15:12]), .in1(ram_1_data_2[27:24]), .out(multiplexer_2_out), .sel(rom_1_data[9]));
  Clock clock_2 (.out(clock_2_out));
  not not_2 (not_2_out, clock_2_out);
  register_file register_file_1 (
    .write_data(multiplexer_6_out), .write_address(ram_1_data_2[27:24]),
    .read_data_0(register_file_1_read_data_0), .read_data_1(register_file_1_read_data_1), .clock(not_2_out),
    .read_address_0(ram_1_data_2[23:20]), .read_address_1(multiplexer_2_out), .write_enable(rom_1_data[0]));
  or or_1 (or_1_out, rom_1_data[7], and_1_out);
  and and_1 (and_1_out, rom_1_data[8], xor_1_out);
  or or_2 (or_2_out, rom_1_data[10], rom_1_data[8]);
  not not_3 (not_3_out, or_2_out);
  Multiplexer #(.width(16), .enable("false")) multiplexer_3 (
    .in0({ram_1_data_2[15:4], ram_1_data}), .in1(multiplexer_4_out), .out(multiplexer_3_out), .sel(not_3_out));
  xor xor_1 (xor_1_out, rom_1_data[10], alu_1_zero);
  xor xor_2 (xor_2_out, ram_1_data_2[16], or_2_out);
  Multiplexer #(.width(16), .enable("false")) multiplexer_4 (
    .in0(register_file_1_read_data_1), .in1({ram_1_data_2[15:4], ram_1_data}), .out(multiplexer_4_out),
    .sel(xor_2_out));
  Multiplexer #(.width(2), .enable("false")) multiplexer_5 (
    .in0(ram_1_data_2[11:10]), .in1(2'b00), .out(multiplexer_5_out), .sel(ram_1_data_2[16]));
  shifter shifter_1 (
    .data_in(multiplexer_4_out), .shift_type(multiplexer_5_out), .shift_amount(ram_1_data),
    .data_out(shifter_1_data_out));
  Multiplexer #(.width(16), .enable("false")) multiplexer_6 (
    .in0(multiplexer_7_out), .in1(bit_extender_2_out), .out(multiplexer_6_out), .sel(and_3_out));
  Multiplexer #(.width(16), .enable("false")) multiplexer_7 (
    .in0(multiplexer_8_out), .in1(adder_1_out), .out(multiplexer_7_out), .sel(ram_1_data_2[17]));
  alu alu_1 (
    .a(register_file_1_read_data_0), .b(shifter_1_data_out), .result(alu_1_result), .zero(alu_1_zero),
    .a_invert(rom_1_data[1]), .carry_in(rom_1_data[3]), .operation(rom_1_data[6:4]), .b_invert(rom_1_data[2]));
  Clock clock_3 (.out(clock_3_out));
  not not_4 (not_4_out, clock_3_out);
  Multiplexer #(.width(16), .enable("false")) multiplexer_8 (
    .in0(alu_1_result), .in1(memory_controller_1_p15), .out(multiplexer_8_out), .sel(rom_1_data[13]));
  Bit_Extender #(.in_width(16), .out_width(7)) bit_extender_1 (
    .in(register_file_1_read_data_1), .out(bit_extender_1_out));
  not not_5 (not_5_out, clock_4_out);
  Clock clock_4 (.out(clock_4_out));
  Clock clock_5 (.out(clock_5_out));
  Comparator #(.width(16), .mode("unsigned")) comparator_2 (
    .a(alu_1_result), .b(16'hff10), .eq(comparator_2_eq));  // open: gt, lt
  Comparator #(.width(16), .mode("unsigned")) comparator_3 (
    .a(alu_1_result), .b(16'hff20), .eq(comparator_3_eq));  // open: gt, lt
  TTY tty_1 (.data(bit_extender_1_out), .clk(not_5_out), .we(and_2_out));  // open: clr
  Keyboard keyboard_1 (.clk(clock_5_out), .re(and_3_out), .data(keyboard_1_data));  // open: clr, avail
  and and_2 (and_2_out, memory_controller_1_p1, comparator_2_eq);
  and and_3 (and_3_out, rom_1_data[13], comparator_3_eq);
  RAM #(.addrWidth(14), .dataWidth(32), .bus("separate")) ram_2 (
    .addr(memory_controller_1_p3), .din(memory_controller_1_p2), .data(ram_2_data),
    .str(memory_controller_1_p9), .sel(memory_controller_1_p10), .clk(memory_controller_1_p11),
    .ld(memory_controller_1_p12), .clr(memory_controller_1_p13));
  // memory_controller memory_controller_1: pin names not known; wires that end beside it: memory_controller_1_p1, memory_controller_1_p2, memory_controller_1_p3, not_4_out, alu_1_result, register_file_1_read_data_1, rom_1_data[11], rom_1_data[12], memory_controller_1_p9, memory_controller_1_p10, memory_controller_1_p11, memory_controller_1_p12, memory_controller_1_p13, ram_2_data, memory_controller_1_p15
  assign bit_extender_2_out = {{9{1'b0}}, keyboard_1_data};  // Bit_Extender bit_extender_2

  // Notes on the sheet:
  //   Program
  //   Counter
  //   Instruction Memory
  //   Leave these pins disconnected
  //   opcode
  //   r1
  //   r2
  //   iformat?
  //   immediate
  //   shift type
  //   shift amt
  //   link
  //   r0
  //   Split this output into the control
  //   signals for your datapath
  //   WriteEnable
  //   contents of rom_1 (hex, n*v repeats v):
  //   1 d 11 21 27 17 31 41 51 2001 3001 a00 1a00 30c 70c 81
  //   AInvert
  //   BInvert
  //   CInvert
  //   ALUOp
  //   Jump
  //   Branch
  //   Read r0
  //   Branch Inv
  //   MemWrite
  //   MemtoReg
  //   Choose Word
  //   Data Memory
endmodule

module register_file (
  input  clock,
  input  write_enable,
  input  [3:0] write_address,
  input  [15:0] write_data,
  input  [3:0] read_address_0,
  input  [3:0] read_address_1,
  output [15:0] read_data_0,
  output [15:0] read_data_1
);

  wire and_1_out, decoder_1_out1, decoder_1_out2, decoder_1_out3, decoder_1_out4, decoder_1_out5,
       decoder_1_out6, decoder_1_out7, decoder_1_out8, decoder_1_out9, decoder_1_out10, decoder_1_out11,
       decoder_1_out12, decoder_1_out13, decoder_1_out14, decoder_1_out15;
  wire [15:0] a0_q, a1_q, a2_q, a3_q, ra_q, s0_q, s1_q, s2_q, s3_q, sp_q, t0_q, t1_q, t2_q, t3_q, v0_q;

  Decoder #(.select(4)) decoder_1 (
    .out1(decoder_1_out1), .out2(decoder_1_out2), .out3(decoder_1_out3), .out4(decoder_1_out4),
    .out5(decoder_1_out5), .out6(decoder_1_out6), .out7(decoder_1_out7), .out8(decoder_1_out8),
    .out9(decoder_1_out9), .out10(decoder_1_out10), .out11(decoder_1_out11), .out12(decoder_1_out12),
    .out13(decoder_1_out13), .out14(decoder_1_out14), .out15(decoder_1_out15), .sel(write_address));  // open: out0, en
  and and_1 (and_1_out, clock, write_enable);
  Register #(.width(16)) v0 (.D(write_data), .en(decoder_1_out1), .Q(v0_q), .clk(and_1_out));  // open: clr
  Register #(.width(16)) a0 (.D(write_data), .en(decoder_1_out2), .Q(a0_q), .clk(and_1_out));  // open: clr
  Register #(.width(16)) a1 (.D(write_data), .en(decoder_1_out3), .Q(a1_q), .clk(and_1_out));  // open: clr
  Register #(.width(16)) a2 (.D(write_data), .en(decoder_1_out4), .Q(a2_q), .clk(and_1_out));  // open: clr
  Register #(.width(16)) a3 (.D(write_data), .en(decoder_1_out5), .Q(a3_q), .clk(and_1_out));  // open: clr
  Register #(.width(16)) t0 (.D(write_data), .en(decoder_1_out6), .Q(t0_q), .clk(and_1_out));  // open: clr
  Register #(.width(16)) t1 (.D(write_data), .en(decoder_1_out7), .Q(t1_q), .clk(and_1_out));  // open: clr
  Register #(.width(16)) t2 (.D(write_data), .en(decoder_1_out8), .Q(t2_q), .clk(and_1_out));  // open: clr
  Register #(.width(16)) t3 (.D(write_data), .en(decoder_1_out9), .Q(t3_q), .clk(and_1_out));  // open: clr
  Register #(.width(16)) s0 (.D(write_data), .en(decoder_1_out10), .Q(s0_q), .clk(and_1_out));  // open: clr
  Register #(.width(16)) s1 (.D(write_data), .en(decoder_1_out11), .Q(s1_q), .clk(and_1_out));  // open: clr
  Register #(.width(16)) s2 (.D(write_data), .en(decoder_1_out12), .Q(s2_q), .clk(and_1_out));  // open: clr
  Register #(.width(16)) s3 (.D(write_data), .en(decoder_1_out13), .Q(s3_q), .clk(and_1_out));  // open: clr
  Register #(.width(16)) sp (.D(write_data), .en(decoder_1_out14), .Q(sp_q), .clk(and_1_out));  // open: clr
  Register #(.width(16)) ra (.D(write_data), .en(decoder_1_out15), .Q(ra_q), .clk(and_1_out));  // open: clr
  Multiplexer #(.select(4), .width(16), .enable("false")) multiplexer_1 (
    .in0({16{1'b0}}), .in1(v0_q), .in2(a0_q), .in3(a1_q), .in4(a2_q), .in5(a3_q), .in6(t0_q), .in7(t1_q),
    .in8(t2_q), .in9(t3_q), .in10(s0_q), .in11(s1_q), .in12(s2_q), .in13(s3_q), .in14(sp_q), .in15(ra_q),
    .out(read_data_0), .sel(read_address_0));
  Multiplexer #(.select(4), .width(16), .enable("false")) multiplexer_2 (
    .in0({16{1'b0}}), .in1(v0_q), .in2(a0_q), .in3(a1_q), .in4(a2_q), .in5(a3_q), .in6(t0_q), .in7(t1_q),
    .in8(t2_q), .in9(t3_q), .in10(s0_q), .in11(s1_q), .in12(s2_q), .in13(s3_q), .in14(sp_q), .in15(ra_q),
    .out(read_data_1), .sel(read_address_1));
endmodule

module alu (
  input  a_invert,
  input  carry_in,
  input  [2:0] operation,
  input  [15:0] a,
  input  [15:0] b,
  input  b_invert,
  output [15:0] result,
  output zero
);

  wire comparator_1_lt, comparator_2_lt;
  wire [15:0] adder_1_out, and_1_out, bit_extender_1_out, bit_extender_2_out, multiplexer_1_out,
       multiplexer_2_out, not_1_out, not_2_out, or_1_out, xor_1_out;

  assign not_1_out = ~a;  // NOT_Gate not_1, 16 bits wide
  assign not_2_out = ~b;  // NOT_Gate not_2, 16 bits wide
  Multiplexer #(.width(16), .enable("false")) multiplexer_1 (
    .in0(a), .in1(not_1_out), .out(multiplexer_1_out), .sel(a_invert));
  Multiplexer #(.width(16), .enable("false")) multiplexer_2 (
    .in0(b), .in1(not_2_out), .out(multiplexer_2_out), .sel(b_invert));
  Adder #(.width(16)) adder_1 (
    .a(multiplexer_1_out), .b(multiplexer_2_out), .out(adder_1_out), .cin(carry_in));  // open: cout
  assign and_1_out = multiplexer_1_out & multiplexer_2_out;  // AND_Gate and_1, 16 bits wide
  assign or_1_out = multiplexer_1_out | multiplexer_2_out;  // OR_Gate or_1, 16 bits wide
  assign xor_1_out = multiplexer_1_out ^ multiplexer_2_out;  // XOR_Gate xor_1, 16 bits wide
  Comparator #(.width(16)) comparator_1 (
    .a(multiplexer_1_out), .b(multiplexer_2_out), .lt(comparator_1_lt));  // open: gt, eq
  Comparator #(.width(16), .mode("unsigned")) comparator_2 (
    .a(multiplexer_1_out), .b(multiplexer_2_out), .lt(comparator_2_lt));  // open: gt, eq
  assign bit_extender_1_out = {{15{1'b0}}, comparator_1_lt};  // Bit_Extender bit_extender_1
  assign bit_extender_2_out = {{15{1'b0}}, comparator_2_lt};  // Bit_Extender bit_extender_2
  Multiplexer #(.select(3), .width(16), .enable("false")) multiplexer_3 (
    .in0(adder_1_out), .in1(and_1_out), .in2(or_1_out), .in3(xor_1_out), .in4(bit_extender_1_out),
    .in5(bit_extender_2_out), .out(result), .sel(operation));  // open: in6, in7
  Comparator #(.width(16)) comparator_3 (.a(result), .b({16{1'b0}}), .eq(zero));  // open: gt, lt
endmodule

module shifter (
  input  [15:0] data_in,
  input  [1:0] shift_type,
  input  [3:0] shift_amount,
  output [15:0] data_out
);

  wire [15:0] shifter_1_out, shifter_2_out, shifter_3_out;

  Shifter #(.width(16)) shifter_1 (.in(data_in), .\dist (shift_amount), .out(shifter_1_out));
  Shifter #(.width(16), .shift("lr")) shifter_2 (.in(data_in), .\dist (shift_amount), .out(shifter_2_out));
  Shifter #(.width(16), .shift("ar")) shifter_3 (.in(data_in), .\dist (shift_amount), .out(shifter_3_out));
  Multiplexer #(.select(2), .width(16), .enable("false")) multiplexer_1 (
    .in0(data_in), .in1(shifter_1_out), .in2(shifter_2_out), .in3(shifter_3_out), .out(data_out),
    .sel(shift_type));
endmodule
